// Logisim project ALU.circ as structural Verilog: 1 circuit, main circuit main
module main (
  input  [9:0] A,
  input  [9:0] B,
  input  [2:0] Select,
  output [9:0] Output
);

  wire [9:0] adder_1_out, and_1_out, divider_1_out, multiplier_1_out, or_1_out, subtractor_1_out, xor_1_out;

  assign and_1_out = A & B;  // AND_Gate and_1, 10 bits wide
  assign or_1_out = A | B;  // OR_Gate or_1, 10 bits wide
  assign xor_1_out = A ^ B;  // XOR_Gate xor_1, 10 bits wide
  Adder #(.width(10)) adder_1 (.a(A), .b(B), .out(adder_1_out));  // open: cin, cout
  Subtractor #(.width(10)) subtractor_1 (.a(A), .b(B), .out(subtractor_1_out));  // open: bin, bout
  Multiplier #(.width(10)) multiplier_1 (.a(A), .b(B), .out(multiplier_1_out));  // open: cin, cout
  Divider #(.width(10)) divider_1 (.a(A), .b(B), .out(divider_1_out));  // open: upper, rem
  Multiplexer #(.select(3), .width(10), .enable("false")) multiplexer_1 (
    .in0(and_1_out), .in1(or_1_out), .in2(xor_1_out), .in3(adder_1_out), .in4(subtractor_1_out),
    .in5(multiplier_1_out), .in6(divider_1_out), .in7({10{1'b0}}), .out(Output), .sel(Select));
endmodule
