// Logisim project CPU.circ as structural Verilog: 1 circuit, main circuit main
module main (
  input  On_Off
);

  wire A, and_1_out, and_2_out, B, clock_1_out, decoder_1_out0, decoder_1_out1, decoder_1_out2,
       decoder_1_out3, LS, Memory, not_1_out, not_2_out, RegIN, REGW, Reset, RW;
  wire [1:0] RS, RT;
  wire [2:0] ALU_Select;
  wire [9:0] adder_1_out, bit_extender_1_out, bit_extender_2_out, main_2_output, multiplexer_1_out,
       multiplexer_2_out, multiplexer_3_out, multiplexer_4_out, multiplexer_5_out, multiplexer_6_out,
       multiplexer_7_out, multiplexer_8_out, ram_1_data, register_1_q, register_2_q, register_3_q,
       register_4_q, register_5_q;
  wire [9:4] rom_1_data;

  Adder #(.width(10)) adder_1 (.a(register_1_q), .b(10'h1), .out(adder_1_out));  // open: cin, cout
  Register #(.width(10)) register_1 (.D(adder_1_out), .Q(register_1_q), .clk(and_1_out), .clr(Reset));  // open: en
  Button u_Reset (.out(Reset));
  ROM #(.addrWidth(10), .dataWidth(10)) rom_1 (.addr(register_1_q), .data({rom_1_data, RS, RT}));  // open: sel
  and and_1 (and_1_out, On_Off, clock_1_out);
  Decoder #(.select(2), .enable("false")) decoder_1 (
    .out0(decoder_1_out0), .out1(decoder_1_out1), .out2(decoder_1_out2), .out3(decoder_1_out3),
    .sel(rom_1_data[5:4]));
  Clock clock_1 (.out(clock_1_out));
  CU_main main_1 (
    .ALU_Select(ALU_Select), .B(B), .RegIN(RegIN), .RW(RW), .A(A), .OP_Code(rom_1_data[9:6]), .LS(LS),
    .Memory(Memory), .RegIN_2(REGW));
  and and_2 (and_2_out, REGW, and_1_out);
  assign bit_extender_1_out = {{8{1'b0}}, RT};  // Bit_Extender bit_extender_1
  Register #(.width(10)) register_2 (
    .D(multiplexer_1_out), .en(decoder_1_out0), .Q(register_2_q), .clk(and_2_out), .clr(Reset));
  Register #(.width(10)) register_3 (
    .D(multiplexer_1_out), .en(decoder_1_out1), .Q(register_3_q), .clk(and_2_out), .clr(Reset));
  Register #(.width(10)) register_4 (
    .D(multiplexer_1_out), .en(decoder_1_out2), .Q(register_4_q), .clk(and_2_out), .clr(Reset));
  Register #(.width(10)) register_5 (
    .D(multiplexer_1_out), .en(decoder_1_out3), .Q(register_5_q), .clk(and_2_out), .clr(Reset));
  Multiplexer #(.width(10), .enable("false")) multiplexer_1 (
    .in0(main_2_output), .in1(ram_1_data), .out(multiplexer_1_out), .sel(RegIN));
  Multiplexer #(.select(2), .width(10), .enable("false")) multiplexer_2 (
    .in0(register_2_q), .in1(register_3_q), .in2(register_4_q), .in3(register_5_q), .out(multiplexer_2_out),
    .sel(RS));
  Multiplexer #(.select(2), .width(10), .enable("false")) multiplexer_3 (
    .in0(register_2_q), .in1(register_3_q), .in2(register_4_q), .in3(register_5_q), .out(multiplexer_3_out),
    .sel(RT));
  Multiplexer #(.select(2), .width(10), .enable("false")) multiplexer_4 (
    .in0(register_2_q), .in1(register_3_q), .in2(register_4_q), .in3(register_5_q), .out(multiplexer_4_out),
    .sel(rom_1_data[5:4]));
  Multiplexer #(.width(10), .enable("false")) multiplexer_5 (
    .in0({RS, {8{1'b0}}}), .in1(multiplexer_2_out), .out(multiplexer_5_out), .sel(A));
  Multiplexer #(.width(10), .enable("false")) multiplexer_6 (
    .in0(bit_extender_1_out), .in1(multiplexer_3_out), .out(multiplexer_6_out), .sel(B));
  Multiplexer #(.width(10), .enable("false")) multiplexer_7 (
    .in0(multiplexer_3_out), .in1(multiplexer_4_out), .out(multiplexer_7_out), .sel(not_1_out));
  not not_1 (not_1_out, LS);
  assign bit_extender_2_out = {{6{1'b0}}, {RS, RT}};  // Bit_Extender bit_extender_2
  Multiplexer #(.width(10), .enable("false")) multiplexer_8 (
    .in0(bit_extender_2_out), .in1(main_2_output), .out(multiplexer_8_out), .sel(LS));
  ALU_main main_2 (.Output(main_2_output), .A(multiplexer_5_out), .B(multiplexer_6_out), .Select(ALU_Select));
  RAM #(.addrWidth(10), .dataWidth(10)) ram_1 (
    .addr(multiplexer_8_out), .data(ram_1_data), .sel(Memory), .clk(and_1_out), .ld(RW), .clr(Reset));
  assign ram_1_data = not_2_out ? multiplexer_7_out : 10'bz;  // Controlled_Buffer controlled_buffer_1
  not not_2 (not_2_out, RW);

  // Notes on the sheet:
  //   contents of rom_1 (hex, n*v repeats v):
  //   240 10*1c3 300 240 1c2 301 240 1c1 302 2c0 2d1 2e2 f1 169 102 13c 330 2c0
endmodule
