// Logisim project CU.circ as structural Verilog: 1 circuit, main circuit main
module main (
  input  [3:0] OP_Code,
  output [2:0] ALU_Select,
  output B,
  output RW,
  output RegIN,
  output Memory,
  output RegIN_2,
  output A,
  output LS
);

  wire decoder_1_out1, decoder_1_out2, decoder_1_out3, decoder_1_out4, decoder_1_out5, decoder_1_out6,
       decoder_1_out15, decoder_2_out11, decoder_2_out12, decoder_3_out12, decoder_3_out13, or_2_out;

  Decoder #(.select(4), .enable("false")) decoder_1 (
    .out1(decoder_1_out1), .out2(decoder_1_out2), .out3(decoder_1_out3), .out4(decoder_1_out4),
    .out5(decoder_1_out5), .out6(decoder_1_out6), .out15(decoder_1_out15), .sel(OP_Code));  // open: out0, out7, out8, out9, out10, out11, out12, out13, out14
  Decoder #(.select(4), .enable("false")) decoder_2 (
    .out11(decoder_2_out11), .out12(decoder_2_out12), .sel(OP_Code));  // open: out0, out1, out2, out3, out4, out5, out6, out7, out8, out9, out10, out13, out14, out15
  not not_1 (A, decoder_2_out12);
  or or_1 (B, decoder_1_out1, decoder_1_out2, decoder_1_out3, decoder_1_out4, decoder_1_out5, decoder_1_out6, decoder_1_out15);
  or or_2 (or_2_out, decoder_2_out11, decoder_2_out12);
  not not_2 (LS, or_2_out);
  Multiplexer #(.select(4), .width(3), .enable("false")) multiplexer_1 (
    .in0(3'b011), .in1(3'b000), .in2(3'b001), .in3(3'b011), .in4(3'b100), .in5(3'b101), .in6(3'b110),
    .in7(3'b011), .in8(3'b100), .in9(3'b101), .in10(3'b110), .in11(3'b011), .in12(3'b011), .in13(3'b011),
    .in14(3'b001), .in15(3'b010), .out(ALU_Select), .sel(OP_Code));
  Decoder #(.select(4), .enable("false")) decoder_3 (
    .out11(RegIN), .out12(decoder_3_out12), .out13(decoder_3_out13), .sel(OP_Code));  // open: out0, out1, out2, out3, out4, out5, out6, out7, out8, out9, out10, out14, out15
  or or_3 (Memory, RegIN, decoder_3_out12);
  not not_3 (RegIN_2, decoder_3_out12);
  or or_4 (RW, RegIN, decoder_3_out13);
endmodule
