// Logisim project Project_ver2.circ as structural Verilog: 5 circuits, main circuit main
module main (
  input  in_1,
  output Overflow,
  output Borrow,
  output [9:0] out_4,
  output [9:0] out_5,
  output [9:0] out_6
);

  wire ALUSrc, Clock, MemRead, MemtoReg, MemWrite, On_Off_out, RegDst, RegWrite, Reset;
  wire [1:0] multiplexer_1_out;
  wire [3:0] Alu_Control, Shmt;
  wire [9:0] adder_1_out, bit_extender_1_out, n10_bit_alu_1_result, ram_1_data, register_1_q,
       register_file_1_read_data_2, rom_1_data;

  Clock clock_1 (.out(Clock));
  Register #(.width(10)) register_1 (.D(adder_1_out), .en(in_1), .Q(register_1_q), .clk(Clock), .clr(Reset));
  not not_1 (Reset, On_Off_out);
  and On_Off (On_Off_out, in_1, in_1);
  Adder #(.width(10)) adder_1 (.a(register_1_q), .b(10'h1), .out(adder_1_out));  // open: cin, cout
  ROM #(.addrWidth(10), .dataWidth(10)) rom_1 (
    .addr(register_1_q), .data({rom_1_data[9:6], Shmt, rom_1_data[1:0]}));  // open: sel
  Multiplexer #(.width(2), .enable("false")) multiplexer_1 (
    .in0(Shmt[1:0]), .in1(rom_1_data[1:0]), .out(multiplexer_1_out), .sel(RegDst));
  Control control_1 (
    .ReDst(RegDst), .ALUSrc(ALUSrc), .MemtoReg(MemtoReg), .RegWrite(RegWrite), .MemRead(MemRead),
    .MemWrite(MemWrite), .ALUOp(Alu_Control), .in_1(rom_1_data[9:6]));
  Register_File register_file_1 (
    .RegWrite(RegWrite), .Read_Data_1(out_4), .Read_Data_2(register_file_1_read_data_2), .Write_Data(out_6),
    .Write_Reg(multiplexer_1_out), .CLOCK(Clock), .Read_Reg_1(Shmt[3:2]), .Read_Reg_2(Shmt[1:0]));
  assign bit_extender_1_out = {{8{1'b0}}, rom_1_data[1:0]};  // Bit_Extender bit_extender_1
  Multiplexer #(.width(10), .enable("false")) multiplexer_2 (
    .in0(register_file_1_read_data_2), .in1(bit_extender_1_out), .out(out_5), .sel(ALUSrc));
  _10_Bit_ALU u_10_bit_alu_1 (
    .Carry(Overflow), .Result(n10_bit_alu_1_result), .Borrow(Borrow), .Shmt(Shmt), .Operand_A(out_4),
    .Operand_B(out_5), .Operation(Alu_Control));  // open: Carry_In
  RAM #(.addrWidth(10), .dataWidth(10), .bus("separate")) ram_1 (
    .addr(n10_bit_alu_1_result), .din(register_file_1_read_data_2), .data(ram_1_data), .str(MemWrite),
    .clk(Clock), .ld(MemRead), .clr(Reset));  // open: sel
  Multiplexer #(.width(10), .enable("false")) multiplexer_3 (
    .in0(n10_bit_alu_1_result), .in1(ram_1_data), .out(out_6), .sel(MemtoReg));

  // Other names for the same wires on the sheet: D1[9:0] = out_4; D2[9:0] = out_5; M2R[9:0] = out_6

  // Notes on the sheet:
  //   contents of rom_1 (hex, n*v repeats v):
  //   389 39d 39 27 79 f9 b9 3eb 226 2a5 189 1c9 2e7 16d 2ed 1c9
endmodule

module _10_Bit_ALU (
  input  Carry_In,
  input  [9:0] Operand_A,
  input  [9:0] Operand_B,
  input  [3:0] Shmt,
  input  [3:0] Operation,
  output Carry,
  output Borrow,
  output [9:0] Result
);

  wire [9:0] adder_1_out, adder_2_out, adder_3_out, adder_4_out, and_1_out, and_2_out, nand_1_out, nor_1_out,
       or_1_out, or_2_out, shifter_1_out, shifter_2_out, subtractor_1_out, subtractor_2_out, xnor_1_out,
       xor_1_out;

  Adder #(.width(10)) adder_1 (.a(Operand_A), .b(Operand_B), .out(adder_1_out), .cin(Carry_In), .cout(Carry));
  Subtractor #(.width(10)) subtractor_1 (
    .a(Operand_A), .b(Operand_B), .out(subtractor_1_out), .bin(Carry_In), .bout(Borrow));
  assign and_1_out = Operand_A & Operand_B;  // AND_Gate and_1, 10 bits wide
  assign or_1_out = Operand_A | Operand_B;  // OR_Gate or_1, 10 bits wide
  assign xor_1_out = Operand_A ^ Operand_B;  // XOR_Gate xor_1, 10 bits wide
  assign nor_1_out = ~(Operand_A | Operand_B);  // NOR_Gate nor_1, 10 bits wide
  Shifter #(.width(10)) shifter_1 (.in(Operand_A), .\dist (Shmt), .out(shifter_1_out));
  Shifter #(.width(10), .shift("lr")) shifter_2 (.in(Operand_A), .\dist (Shmt), .out(shifter_2_out));
  Adder #(.width(10)) adder_2 (.a(Operand_A), .b(Operand_B), .out(adder_2_out), .cin(Carry_In));  // open: cout
  Subtractor #(.width(10)) subtractor_2 (
    .a(Operand_A), .b(Operand_B), .out(subtractor_2_out), .bin(Carry_In));  // open: bout
  assign and_2_out = Operand_A & Operand_B;  // AND_Gate and_2, 10 bits wide
  assign or_2_out = Operand_A | Operand_B;  // OR_Gate or_2, 10 bits wide
  assign xnor_1_out = ~(Operand_A ^ Operand_B);  // XNOR_Gate xnor_1, 10 bits wide
  assign nand_1_out = ~(Operand_A & Operand_B);  // NAND_Gate nand_1, 10 bits wide
  Adder #(.width(10)) adder_3 (.a(Operand_A), .b(Operand_B), .out(adder_3_out));  // open: cin, cout
  Adder #(.width(10)) adder_4 (.a(Operand_A), .b(Operand_B), .out(adder_4_out));  // open: cin, cout
  Multiplexer #(.select(4), .width(10), .enable("false")) multiplexer_1 (
    .in0(adder_1_out), .in1(subtractor_1_out), .in2(and_1_out), .in3(or_1_out), .in4(xor_1_out),
    .in5(nor_1_out), .in6(shifter_1_out), .in7(shifter_2_out), .in8(adder_2_out), .in9(subtractor_2_out),
    .in10(and_2_out), .in11(or_2_out), .in12(xnor_1_out), .in13(nand_1_out), .in14(adder_3_out),
    .in15(adder_4_out), .out(Result), .sel(Operation));
endmodule

module Register_File (
  input  [9:0] Write_Data,
  input  RegWrite,
  input  [1:0] Read_Reg_1,
  input  [1:0] Write_Reg,
  input  [1:0] Read_Reg_2,
  input  CLOCK,
  output [9:0] Read_Data_1,
  output [9:0] Read_Data_2
);

  wire decoder_1_out0, decoder_1_out1, decoder_1_out2, decoder_1_out3;
  wire [9:0] register_1_q, register_2_q, register_3_q, register_4_q;

  Decoder #(.select(2)) decoder_1 (
    .out0(decoder_1_out0), .out1(decoder_1_out1), .out2(decoder_1_out2), .out3(decoder_1_out3),
    .sel(Write_Reg), .en(RegWrite));
  Register #(.width(10)) register_1 (.D(Write_Data), .en(decoder_1_out0), .Q(register_1_q), .clk(CLOCK));  // open: clr
  Register #(.width(10)) register_2 (.D(Write_Data), .en(decoder_1_out1), .Q(register_2_q), .clk(CLOCK));  // open: clr
  Register #(.width(10)) register_3 (.D(Write_Data), .en(decoder_1_out2), .Q(register_3_q), .clk(CLOCK));  // open: clr
  Register #(.width(10)) register_4 (.D(Write_Data), .en(decoder_1_out3), .Q(register_4_q), .clk(CLOCK));  // open: clr
  Multiplexer #(.select(2), .width(10)) multiplexer_1 (
    .in0(register_1_q), .in1(register_2_q), .in2(register_3_q), .in3(register_4_q), .out(Read_Data_1),
    .sel(Read_Reg_1));  // open: en
  Multiplexer #(.select(2), .width(10)) multiplexer_2 (
    .in0(register_1_q), .in1(register_2_q), .in2(register_3_q), .in3(register_4_q), .out(Read_Data_2),
    .sel(Read_Reg_2));  // open: en
endmodule

module Control (
  input  [3:0] in_1,
  output ReDst,
  output ALUSrc,
  output MemtoReg,
  output RegWrite,
  output MemRead,
  output MemWrite,
  output [3:0] ALUOp
);

  wire not_2_out, not_3_out;

  not not_1 (ReDst, in_1[3]);
  not not_2 (not_2_out, in_1[3]);
  not not_3 (not_3_out, in_1[0]);
  and and_1 (MemRead, in_1[3], in_1[2], in_1[1], not_3_out);
  and and_2 (MemWrite, in_1[3], in_1[2], in_1[1], in_1[0]);
  or or_1 (RegWrite, not_2_out, MemRead);

  assign ALUOp = in_1;
  assign ALUSrc = in_1[3];
  assign MemtoReg = MemRead;
endmodule

module debug (
  input  [9:0] in_1,
  input  in_2,
  output [9:0] out_3,
  output [9:0] out_4,
  output Overflow,
  output Borrow,
  output [9:0] out_7,
  output [1:0] out_8,
  output [1:0] out_9,
  output [1:0] out_10,
  output [3:0] out_11
);

  wire ALUSrc, Clock, decoder_1_out0, decoder_1_out1, decoder_1_out2, decoder_1_out3, MemRead, MemtoReg,
       MemWrite, On_Off_out, RegDst, RegWrite, Reset;
  wire [1:0] RW;
  wire [3:0] Alu_Control;
  wire [9:0] adder_1_out, bit_extender_1_out, multiplexer_3_out, multiplexer_5_out, ram_1_data, register_1_q,
       register_2_q, register_3_q, register_4_q, register_5_q;
  wire [9:6] rom_1_data;

  Clock clock_1 (.out(Clock));
  Register #(.width(10)) register_1 (.D(adder_1_out), .en(in_2), .Q(register_1_q), .clk(Clock), .clr(Reset));
  not not_1 (Reset, On_Off_out);
  and On_Off (On_Off_out, in_2, in_2);
  Adder #(.width(10)) adder_1 (.a(register_1_q), .b(in_1), .out(adder_1_out));  // open: cin, cout
  ROM #(.addrWidth(10), .dataWidth(10)) rom_1 (
    .addr(register_1_q), .data({rom_1_data, out_8, out_9, out_10}));  // open: sel
  Control control_1 (
    .ReDst(RegDst), .ALUSrc(ALUSrc), .MemtoReg(MemtoReg), .RegWrite(RegWrite), .MemRead(MemRead),
    .MemWrite(MemWrite), .ALUOp(Alu_Control), .in_1(rom_1_data));
  Multiplexer #(.width(2), .enable("false")) multiplexer_1 (.in0(out_9), .in1(out_10), .out(RW), .sel(RegDst));
  Decoder #(.select(2)) decoder_1 (
    .out0(decoder_1_out0), .out1(decoder_1_out1), .out2(decoder_1_out2), .out3(decoder_1_out3), .sel(RW),
    .en(RegWrite));
  assign bit_extender_1_out = {{8{1'b0}}, out_10};  // Bit_Extender bit_extender_1
  Register #(.width(10)) register_2 (
    .D(multiplexer_5_out), .en(decoder_1_out0), .Q(register_2_q), .clk(Clock));  // open: clr
  Register #(.width(10)) register_3 (
    .D(multiplexer_5_out), .en(decoder_1_out1), .Q(register_3_q), .clk(Clock));  // open: clr
  Register #(.width(10)) register_4 (
    .D(multiplexer_5_out), .en(decoder_1_out2), .Q(register_4_q), .clk(Clock));  // open: clr
  Register #(.width(10)) register_5 (
    .D(multiplexer_5_out), .en(decoder_1_out3), .Q(register_5_q), .clk(Clock));  // open: clr
  Multiplexer #(.select(2), .width(10), .enable("false")) multiplexer_2 (
    .in0(register_2_q), .in1(register_3_q), .in2(register_4_q), .in3(register_5_q), .out(out_3), .sel(out_8));
  Multiplexer #(.select(2), .width(10), .enable("false")) multiplexer_3 (
    .in0(register_2_q), .in1(register_3_q), .in2(register_4_q), .in3(register_5_q), .out(multiplexer_3_out),
    .sel(out_9));
  Multiplexer #(.width(10), .enable("false")) multiplexer_4 (
    .in0(multiplexer_3_out), .in1(bit_extender_1_out), .out(out_4), .sel(ALUSrc));
  _10_Bit_ALU u_10_bit_alu_1 (
    .Carry(Overflow), .Result(out_7), .Borrow(Borrow), .Shmt({out_8, out_9}), .Operand_A(out_3),
    .Operand_B(out_4), .Operation(Alu_Control));  // open: Carry_In
  RAM #(.addrWidth(10), .dataWidth(10), .bus("separate")) ram_1 (
    .addr(out_7), .din(multiplexer_3_out), .data(ram_1_data), .str(MemWrite), .clk(Clock), .ld(MemRead),
    .clr(Reset));  // open: sel
  Multiplexer #(.width(10), .enable("false")) multiplexer_5 (
    .in0(out_7), .in1(ram_1_data), .out(multiplexer_5_out), .sel(MemtoReg));

  assign out_11 = {out_8, out_9};

  // Other names for the same wires on the sheet: R2[1:0] = out_9; Shmt[3:0] = {out_8, out_9}; R1[1:0] = out_8

  // Notes on the sheet:
  //   contents of rom_1 (hex, n*v repeats v):
  //   389 39d 39 27 79 f9 b9 3eb 226 2a5 2e7 16d 2ed 0 4*1b2
endmodule
